// Logisim project Projet.circ as structural Verilog: 6 circuits, main circuit main
// Op
module main (
  input  [15:0] in_1,
  input  in_2
);

  wire jmpCond, not_1_out, RamL, RamW, trueIsJump, xor_1_out;
  wire [1:0] PCupdateSig, SPcsel, SPsel, Wcsel, Wsel;
  wire [2:0] StackInputSel, ual_1_flags;
  wire [3:0] Op;
  wire [5:0] Opcode;
  wire [9:0] valInstr_adrInstr;
  wire [15:0] adrRet, C, extvalInstr_adrInstr, majpc_1_newpc, multiplexer_1_out, PC_1, stack_1_stack_sp_1,
       Stack_SP, test_1_output, valRam;

  ROM #(.addrWidth(16), .dataWidth(16)) rom_1 (.addr(in_1), .data({Opcode, valInstr_adrInstr}));  // open: sel
  RAM #(.addrWidth(16), .dataWidth(16), .bus("separate")) ram_1 (
    .addr(extvalInstr_adrInstr), .din(Stack_SP), .data(valRam), .str(RamW), .clk(in_2), .ld(RamL));  // open: sel, clr
  Multiplexer #(.select(3), .width(16), .enable("false")) multiplexer_1 (
    .in0(Stack_SP), .in1(valRam), .in2(C), .in3(test_1_output), .in4(extvalInstr_adrInstr),
    .out(multiplexer_1_out), .sel(StackInputSel));  // open: in5, in6, in7
  Register #(.width(16)) PC (.D(majpc_1_newpc), .Q(in_1), .clk(in_2));  // open: en, clr
  stack stack_1 (
    .Input(multiplexer_1_out), .SPsel(SPsel), .Wsel(Wsel), .Clock(in_2), .Stack_SP(Stack_SP),
    .Stack_SP_1(stack_1_stack_sp_1));
  not not_1 (not_1_out, xor_1_out);
  xor xor_1 (xor_1_out, trueIsJump, jmpCond);
  majPC majpc_1 (
    .PC(in_1), .PCupdateSig(PCupdateSig), .jmpCond(not_1_out), .PC_1(PC_1), .adrRet(adrRet),
    .adrInstr(extvalInstr_adrInstr), .newPC(majpc_1_newpc));
  UAL ual_1 (.A(Stack_SP), .B(stack_1_stack_sp_1), .Op(Op), .Flags(ual_1_flags), .C(C));  // open: CBout
  test test_1 (.Opcode(Opcode), .Flags(ual_1_flags), .Output(test_1_output));
  controller controller_1 (
    .in_1(Opcode), .Op(Op), .StackInputSel(StackInputSel), .PCupdateSig(PCupdateSig), .halt(trueIsJump),
    .RamW(RamW), .RamL(RamL), .Wcsel(Wcsel), .SPcsel(SPcsel), .Wsel(Wsel), .SPsel(SPsel));
  assign extvalInstr_adrInstr = {{6{1'b0}}, valInstr_adrInstr};  // Bit_Extender bit_extender_1
  BitSelector #(.width(16)) bitselector_1 (.in(Stack_SP), .out(jmpCond), .sel(4'b0000));
  stack stack_2 (.Input(PC_1), .SPsel(SPcsel), .Wsel(Wcsel), .Clock(in_2), .Stack_SP(adrRet));  // open: Stack_SP_1

  // Other names for the same wires on the sheet: Clock = in_2; PC[15:0] = in_1

  // Notes on the sheet:
  //   contents of rom_1 (hex, n*v repeats v):
  //   4409 5000 4401 5001 4401 5002 4401 5003 4400 5004 4801 4800 4401 400 2c00 401d 4802 4803 0 5004 4803
  //   5002 4804 5003 4801 4401 0 5001 540a 6000
endmodule

module UAL (
  input  [3:0] Op,
  input  [15:0] A,
  input  [15:0] B,
  output [15:0] C,
  output [2:0] Flags,
  output CBout
);

  wire A15, add15, and_2_out, and_3_out, and_4_out, and_5_out, and_6_out, and_7_out, and_8_out, and_9_out,
       B15, bitselector_7_out, bitselector_8_out, Borrow, Carry, not_2_out, not_3_out, not_4_out, not_5_out,
       not_6_out, not_7_out, not_8_out, not_9_out, not_10_out, not_11_out, not_12_out, not_13_out,
       not_14_out, not_15_out, not_16_out, not_17_out, not_18_out, not_19_out, not_20_out, not_21_out,
       not_22_out, not_23_out, OFadd, OFsub, sub15;
  wire [3:0] A0123;
  wire [15:0] add, \and , div, mul, neg, \not , \or , rem, shl, sra, sub;

  assign \not  = ~A;  // NOT_Gate not_1, 16 bits wide
  Adder #(.width(16)) adder_1 (.a(B), .b(A), .out(add), .cout(Carry));  // open: cin
  Subtractor #(.width(16)) subtractor_1 (.a(B), .b(A), .out(sub), .bout(Borrow));  // open: bin
  Negator #(.width(16)) negator_1 (.in(A), .out(neg));
  Multiplier #(.width(16)) multiplier_1 (.a(B), .b(A), .out(mul));  // open: cin, cout
  Divider #(.width(16)) divider_1 (.a(B), .b(A), .out(div), .rem(rem));  // open: upper
  assign \and  = B & A;  // AND_Gate and_1, 16 bits wide
  assign \or  = B | A;  // OR_Gate or_1, 16 bits wide
  Shifter #(.width(16)) shifter_1 (.in(B), .\dist (A0123), .out(shl));
  Shifter #(.width(16), .shift("ar")) shifter_2 (.in(B), .\dist (A0123), .out(sra));
  BitSelector #(.width(16)) bitselector_1 (.in(C), .out(Flags[1]), .sel(4'b1111));
  BitSelector #(.width(16)) bitselector_2 (.in(A), .out(A15), .sel(4'b1111));
  BitSelector #(.width(16)) bitselector_3 (.in(B), .out(B15), .sel(4'b1111));
  BitSelector #(.width(16), .group(4)) bitselector_4 (.in(A), .out(A0123), .sel(2'b11));
  BitSelector #(.width(16)) bitselector_5 (.in(add), .out(add15), .sel(4'b1111));
  BitSelector #(.width(16)) bitselector_6 (.in(sub), .out(sub15), .sel(4'b1111));
  not not_2 (not_2_out, A15);
  not not_3 (not_3_out, B15);
  not not_4 (not_4_out, A15);
  not not_5 (not_5_out, B15);
  and and_2 (and_2_out, A15, B15);
  and and_3 (and_3_out, not_2_out, not_3_out);
  and and_4 (and_4_out, not_4_out, B15);
  and and_5 (and_5_out, A15, not_5_out);
  not not_6 (not_6_out, add15);
  and and_6 (and_6_out, not_6_out, and_2_out);
  and and_7 (and_7_out, and_3_out, add15);
  not not_7 (not_7_out, sub15);
  and and_8 (and_8_out, not_7_out, and_4_out);
  and and_9 (and_9_out, and_5_out, sub15);
  or or_2 (OFadd, and_6_out, and_7_out);
  or or_3 (OFsub, and_8_out, and_9_out);
  Multiplexer #(.select(4), .width(16), .enable("false")) multiplexer_1 (
    .in0(add), .in1(sub), .in2(neg), .in3(mul), .in4(div), .in5(rem), .in6(\not ), .in7(\and ), .in8(\or ),
    .in9(shl), .in10(sra), .out(C), .sel(Op));  // open: in11, in12, in13, in14, in15
  Multiplexer #(.enable("false")) multiplexer_2 (.in0(Carry), .in1(Borrow), .out(CBout), .sel(bitselector_7_out));
  BitSelector #(.width(4)) bitselector_7 (.in(Op), .out(bitselector_7_out), .sel(2'b00));
  Multiplexer #(.enable("false")) multiplexer_3 (.in0(OFadd), .in1(OFsub), .out(Flags[2]), .sel(bitselector_8_out));
  BitSelector #(.width(4)) bitselector_8 (.in(Op), .out(bitselector_8_out), .sel(2'b00));
  not not_8 (not_8_out, C[0]);
  not not_9 (not_9_out, C[1]);
  not not_10 (not_10_out, C[2]);
  not not_11 (not_11_out, C[3]);
  not not_12 (not_12_out, C[4]);
  not not_13 (not_13_out, C[5]);
  not not_14 (not_14_out, C[6]);
  not not_15 (not_15_out, C[7]);
  not not_16 (not_16_out, C[8]);
  not not_17 (not_17_out, C[9]);
  not not_18 (not_18_out, C[10]);
  not not_19 (not_19_out, C[11]);
  not not_20 (not_20_out, C[12]);
  not not_21 (not_21_out, C[13]);
  not not_22 (not_22_out, C[14]);
  not not_23 (not_23_out, C[15]);
  and and_10 (Flags[0], not_8_out, not_9_out, not_10_out, not_11_out, not_12_out, not_13_out, not_14_out, not_15_out, not_16_out, not_17_out, not_18_out, not_19_out, not_20_out, not_21_out, not_22_out, not_23_out);

  // Other names for the same wires on the sheet: ZF = Flags[0]; C15 = Flags[1]; SF = Flags[1]; OF = Flags[2]
endmodule

module test (
  input  [2:0] Flags,
  input  [5:0] Opcode,
  output [15:0] Output
);

  wire eq, gt, lt, not_1_out, not_2_out, not_3_out, not_4_out, testState, xor_1_out, xor_2_out;
  wire [1:0] bitselector_1_out, testSelector;

  not not_1 (not_1_out, Flags[0]);
  not not_2 (not_2_out, Flags[1]);
  not not_3 (not_3_out, Flags[2]);
  xor xor_1 (xor_1_out, Flags[2], Flags[1]);
  and and_1 (lt, xor_1_out, not_3_out);
  and and_2 (eq, not_3_out, not_2_out, Flags[0]);
  xor xor_2 (xor_2_out, Flags[2], Flags[1]);
  not not_4 (not_4_out, xor_2_out);
  and and_3 (gt, not_4_out, not_3_out);
  Multiplexer #(.select(2), .enable("false")) multiplexer_1 (
    .in0(gt), .in1(eq), .in2(lt), .out(testState), .sel(testSelector));  // open: in3
  BitSelector #(.width(6), .group(2)) bitselector_1 (.in(Opcode), .out(bitselector_1_out), .sel(2'b00));
  Multiplexer #(.select(2), .width(2), .enable("false")) multiplexer_2 (
    .in0(2'b01), .in1(2'b00), .in3(2'b10), .out(testSelector), .sel(bitselector_1_out));  // open: in2
  assign Output = {{15{1'b0}}, testState};  // Bit_Extender bit_extender_1

  // Other names for the same wires on the sheet: ZF = Flags[0]; SF = Flags[1]; OF = Flags[2]
endmodule

module stack (
  input  [15:0] Input,
  input  [1:0] SPsel,
  input  [1:0] Wsel,
  input  Clock,
  output [15:0] Stack_SP,
  output [15:0] Stack_SP_1
);

  wire wb0, wb1, wb2, wb3, wb4, wb5, wb6, wb7, wb8, wb9, wb10, wb11, wb12, wb13, wb14, wb15, writeBool;
  wire [3:0] adder_1_out, adder_2_out, SPnew, SPval, SPwrite, subtractor_1_out, subtractor_2_out,
       subtractor_3_out;
  wire [15:0] r0, r1, r2, r3, r4, r5, r6, r7, r8, r9, r10, r11, r12, r13, r14, r15, wr0, wr1, wr2, wr3, wr4,
       wr5, wr6, wr7, wr8, wr9, wr10, wr11, wr12, wr13, wr14, wr15;

  Register #(.width(16)) register_1 (.D(wr0), .en(wb0), .Q(r0), .clk(Clock));  // open: clr
  Register #(.width(16)) register_2 (.D(wr1), .en(wb1), .Q(r1), .clk(Clock));  // open: clr
  Register #(.width(16)) register_3 (.D(wr2), .en(wb2), .Q(r2), .clk(Clock));  // open: clr
  Register #(.width(16)) register_4 (.D(wr3), .en(wb3), .Q(r3), .clk(Clock));  // open: clr
  Register #(.width(16)) register_5 (.D(wr4), .en(wb4), .Q(r4), .clk(Clock));  // open: clr
  Register #(.width(16)) register_6 (.D(wr5), .en(wb5), .Q(r5), .clk(Clock));  // open: clr
  Demultiplexer #(.select(4), .width(16), .enable("false")) demultiplexer_1 (
    .out0(wr15), .out1(wr14), .out2(wr13), .out3(wr12), .out4(wr11), .out5(wr10), .out6(wr9), .out7(wr8),
    .out8(wr7), .out9(wr6), .out10(wr5), .out11(wr4), .out12(wr3), .out13(wr2), .out14(wr1), .out15(wr0),
    .in(Input), .sel(SPwrite));
  Demultiplexer #(.select(4), .enable("false")) demultiplexer_2 (
    .out0(wb15), .out1(wb14), .out2(wb13), .out3(wb12), .out4(wb11), .out5(wb10), .out6(wb9), .out7(wb8),
    .out8(wb7), .out9(wb6), .out10(wb5), .out11(wb4), .out12(wb3), .out13(wb2), .out14(wb1), .out15(wb0),
    .in(writeBool), .sel(SPwrite));
  Register #(.width(16)) register_7 (.D(wr6), .en(wb6), .Q(r6), .clk(Clock));  // open: clr
  Register #(.width(16)) register_8 (.D(wr7), .en(wb7), .Q(r7), .clk(Clock));  // open: clr
  Register #(.width(16)) register_9 (.D(wr8), .en(wb8), .Q(r8), .clk(Clock));  // open: clr
  Register #(.width(4)) SP (.D(SPnew), .Q(SPval), .clk(Clock));  // open: en, clr
  Register #(.width(16)) register_10 (.D(wr9), .en(wb9), .Q(r9), .clk(Clock));  // open: clr
  Multiplexer #(.select(4), .width(16), .enable("false")) multiplexer_1 (
    .in0(r15), .in1(r14), .in2(r13), .in3(r12), .in4(r11), .in5(r10), .in6(r9), .in7(r8), .in8(r7), .in9(r6),
    .in10(r5), .in11(r4), .in12(r3), .in13(r2), .in14(r1), .in15(r0), .out(Stack_SP), .sel(SPval));
  Register #(.width(16)) register_11 (.D(wr10), .en(wb10), .Q(r10), .clk(Clock));  // open: clr
  Register #(.width(16)) register_12 (.D(wr11), .en(wb11), .Q(r11), .clk(Clock));  // open: clr
  Register #(.width(16)) register_13 (.D(wr12), .en(wb12), .Q(r12), .clk(Clock));  // open: clr
  Subtractor #(.width(4)) subtractor_1 (.a(SPval), .b(4'b0001), .out(subtractor_1_out));  // open: bin, bout
  Adder #(.width(4)) adder_1 (.a(SPval), .b(4'b0001), .out(adder_1_out));  // open: cin, cout
  Register #(.width(16)) register_14 (.D(wr13), .en(wb13), .Q(r13), .clk(Clock));  // open: clr
  Register #(.width(16)) register_15 (.D(wr14), .en(wb14), .Q(r14), .clk(Clock));  // open: clr
  Register #(.width(16)) register_16 (.D(wr15), .en(wb15), .Q(r15), .clk(Clock));  // open: clr
  Multiplexer #(.select(2), .width(4), .enable("false")) multiplexer_2 (
    .in0(SPval), .in1(adder_1_out), .in2(subtractor_1_out), .in3(4'b0000), .out(SPwrite), .sel(Wsel));
  Multiplexer #(.select(4), .width(16), .enable("false")) multiplexer_3 (
    .in0(r15), .in1(r14), .in2(r13), .in3(r12), .in4(r11), .in5(r10), .in6(r9), .in7(r8), .in8(r7), .in9(r6),
    .in10(r5), .in11(r4), .in12(r3), .in13(r2), .in14(r1), .in15(r0), .out(Stack_SP_1), .sel(subtractor_2_out));
  Subtractor #(.width(4)) subtractor_2 (.a(SPval), .b(4'b0001), .out(subtractor_2_out));  // open: bin, bout
  nand nand_1 (writeBool, Wsel[0], Wsel[1]);
  Subtractor #(.width(4)) subtractor_3 (.a(SPval), .b(4'b0001), .out(subtractor_3_out));  // open: bin, bout
  Adder #(.width(4)) adder_2 (.a(SPval), .b(4'b0001), .out(adder_2_out));  // open: cin, cout
  Multiplexer #(.select(2), .width(4), .enable("false")) multiplexer_4 (
    .in0(4'b0000), .in1(subtractor_3_out), .in2(SPval), .in3(adder_2_out), .out(SPnew), .sel(SPsel));
endmodule

module majPC (
  input  [15:0] PC,
  input  [1:0] PCupdateSig,
  input  jmpCond,
  input  [15:0] adrRet,
  input  [15:0] adrInstr,
  output [15:0] newPC,
  output [15:0] PC_1
);

  wire [15:0] adder_1_out, adder_2_out, multiplexer_1_out;

  Adder #(.width(16)) adder_1 (.a(PC), .b(16'h1), .out(adder_1_out));  // open: cin, cout
  Multiplexer #(.width(16), .enable("false")) multiplexer_1 (
    .in0(adder_1_out), .in1(adrInstr), .out(multiplexer_1_out), .sel(jmpCond));
  Adder #(.width(16)) adder_2 (.a(PC), .b(16'h1), .out(adder_2_out));  // open: cin, cout
  Multiplexer #(.select(2), .width(16), .enable("false")) multiplexer_2 (
    .in0(adrInstr), .in1(multiplexer_1_out), .in2(adrRet), .in3(adder_2_out), .out(newPC), .sel(PCupdateSig));
  Adder #(.width(16)) adder_3 (.a(PC), .b(16'h1), .out(PC_1));  // open: cin, cout
endmodule

module controller (
  input  [5:0] in_1,
  output [3:0] Op,
  output [2:0] StackInputSel,
  output [1:0] PCupdateSig,
  output halt,
  output RamW,
  output RamL,
  output [1:0] Wcsel,
  output [1:0] SPcsel,
  output [1:0] Wsel,
  output [1:0] SPsel
);

  wire [4:0] bitselector_1_out;

  BitSelector #(.width(6), .group(5)) bitselector_1 (.in(in_1), .out(bitselector_1_out), .sel(1'b0));
  Multiplexer #(.select(5), .width(20), .enable("false")) multiplexer_1 (
    .in0(20'h6b1a0), .in1(20'h6b1a1), .in2(20'h8b1a2), .in3(20'h6b1a3), .in4(20'h6b1a4), .in5(20'h6b1a5),
    .in6(20'h8b1a6), .in7(20'h6b1a7), .in8(20'h6b1a8), .in9(20'h6b1a9), .in10(20'h6b1aa), .in11(20'h6b1b1),
    .in12(20'h6b1b1), .in13(20'h6b1b1), .in14(20'hbb000), .in15(20'h7b280), .in16(20'h7b080),
    .in17(20'hdb1c0), .in18(20'hdb990), .in19(20'h7b180), .in20(20'h7b580), .in21(20'hbd000),
    .in22(20'hb7100), .in23(20'hdb180), .in24(20'h33200),
    .out({SPsel, Wsel, SPcsel, Wcsel, RamL, RamW, halt, PCupdateSig, StackInputSel, Op}),
    .sel(bitselector_1_out));  // open: in25, in26, in27, in28, in29, in30, in31

  // Other names for the same wires on the sheet: rawSigData[19:0] = {SPsel, Wsel, SPcsel, Wcsel, RamL, RamW, halt, PCupdateSig, StackInputSel, Op};
  //   Opcode[5:0] = in_1

  // Notes on the sheet:
  //   Mémoire opcode -> opération
endmodule
